# Fritzing sketch partylights (saved by Fritzing 0.9.3b)
breadboards: 1

parts:
  Part1 = maple mini
  R1 = Resistor [tolerance=±5% resistance=220 package="2010 [SMD]"]
  C3 = Ceramic Capacitor [capacitance=10nF package="1206 [SMD, multilayer]"]
  C4 = Ceramic Capacitor [capacitance=10nF package="1206 [SMD, multilayer]"]
  C8 = Capacitor [part_number="33 pF" package=cap-pth-5mm]
  C9 = Ceramic Capacitor [capacitance=100nF package="1206 [SMD, multilayer]"]
  IC3 = MSGEQ7 [package=soic8]
  Part11 = Bluetooth HC-05 Macho  # not connected
  J4 = Basic Servo
  RGB_SMD_LED1 = SMD RGB LED (WS2812) [package=5050]
  RGB_SMD_LED2 = SMD RGB LED (WS2812) [package=5050]
  Part12 = Adafruit MAX9814 Electret Microphone Amplifier [part_number="Adafruit #1713"]
  Part13 = Adafruit AT42QT1012 Standalone Toggle Capacitive Touch Sensor Breakout [part_number="Adafruit #1375"]
  Part14 = Adafruit AT42QT1012 Standalone Toggle Capacitive Touch Sensor Breakout [part_number="Adafruit #1375"]
  Part15 = Adafruit AT42QT1012 Standalone Toggle Capacitive Touch Sensor Breakout [part_number="Adafruit #1375"]
  Part16 = Adafruit AT42QT1012 Standalone Toggle Capacitive Touch Sensor Breakout [part_number="Adafruit #1375"]

nets:
  VDD: Part1.vcc, Part13.VDD, Part14.VDD, Part15.VDD, Part16.VDD
  VDD_2: Part1.vin, R1.Pin_0, C4.0, C9.1, IC3.VDD, J4.vcc, RGB_SMD_LED1.VCC, RGB_SMD_LED1.VDD, RGB_SMD_LED2.VDD, Part12.VDD
  N1: Part1.27, J4.pulse
  N2: Part1.29, Part12.GAIN
  N3: Part1.30, IC3.RESET
  N4: Part1.31, IC3.STROBE
  N5: Part1.4, RGB_SMD_LED1.DIn
  N6: Part1.10, IC3.DCOUT
  N7: Part1.11, Part13.OUT
  N8: Part1.12, Part14.OUT
  N9: Part1.13, Part15.OUT
  N10: Part1.14, Part16.OUT
  GND: Part1.gnd, C4.1, C8.1, IC3.GND, J4.gnd, RGB_SMD_LED1.VSS, RGB_SMD_LED2.VSS, Part12.GND, Part13.GND, Part14.GND, Part15.GND, Part16.GND
  N11: R1.Pin_1, C8.2, IC3.CKIN
  N12: C3.0, IC3.AUDIO_IN
  N13: C3.1, Part12.OUTPUT
  N14: C9.0, IC3.CG
  N15: RGB_SMD_LED1.DOut, RGB_SMD_LED2.DIn

notes:
  .. 61..
  Cycle visualization
  Cycle mic sensitivity
  Freeze color rotation
  Enable "Dance" motion
  5V rail
  3V rail

custom parts:
  Adafruit MAX9814 Electret Microphone Amplifier: Add an ear to your project with this well-designed electret microphone amplifier with AGC. This fully assembled and tested board comes with a 20-20KHz electret microphone soldered on. For the amplification, we use the Maxim MAX9814, a specialty chip that is designed for amplifying electret microphones in situations where the loudness of the audio isn't predictable. This fancy microphone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
  Adafruit AT42QT1012 Standalone Toggle Capacitive Touch Sensor Breakout: This breakout board is the simplest way to create a project with a single "toggle" capacitive touch sensor. No microcontroller is required here - just power with 1.8 to 5.5VDC and touch the pad to activate the sensor. This sensor is a toggle output type: touch-on then touch-off. That means that when a capacitive load is detected (e.g. a person touches the sensor-pad area) the red LED will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
